# Fritzing sketch CourseVoiliers (saved by Fritzing 0.9.3b)
breadboards: 1

parts:
  Composant1 = Arduino Mega 2560 (Rev3)
  Composant2 = Rotoshield - Motor driver shield for Arduino
  M1 = DC Motor
  M2 = DC Motor
  M3 = DC Motor
  R1 = Resistor [tolerance=±5% resistance=10k package=THT]
  S1 = Toggle Switch [package=THT]
  R2 = Resistor [tolerance=±5% resistance=10k package=THT]
  R3 = Resistor [tolerance=±5% resistance=10k package=THT]
  R4 = Resistor [tolerance=±5% resistance=10k package=THT]
  R5 = Resistor [tolerance=±5% resistance=10k package=THT]
  R6 = Resistor [tolerance=±5% resistance=10k package=THT]
  R7 = Resistor [tolerance=±5% resistance=10k package=THT]
  R8 = Resistor [tolerance=±5% resistance=10k package=THT]
  R9 = Resistor [tolerance=±5% resistance=10k package=THT]
  R10 = Resistor [tolerance=±5% resistance=10k package=THT]
  R11 = Resistor [tolerance=±5% resistance=10k package=THT]
  R12 = Resistor [tolerance=±5% resistance=10k package=THT]
  S2 = Toggle Switch [package=THT]
  S3 = Toggle Switch [package=THT]
  S4 = Toggle Switch [package=THT]
  S5 = Toggle Switch [package=THT]
  S6 = Toggle Switch [package=THT]
  S7 = Toggle Switch [package=THT]
  S8 = Toggle Switch [package=THT]
  S9 = Toggle Switch [package=THT]
  S10 = Toggle Switch [package=THT]
  S11 = Toggle Switch [package=THT]
  S12 = Toggle Switch [package=THT]
  S13 = Pushbutton [package=THT]
  R13 = Resistor [tolerance=±5% resistance=10k package=THT]
  Power_plug1 = Power plug
  LED1 = LED - 5mm [color="Green (560nm)" package="5 mm [THT]"]
  R14 = Resistor [tolerance=±5% resistance=470 package=THT]
  LED2 = LED - 5mm [color="Green (560nm)" package="5 mm [THT]"]
  LED3 = LED - 5mm [color="Green (560nm)" package="5 mm [THT]"]
  R15 = Resistor [tolerance=±5% resistance=470 package=THT]
  R16 = Resistor [tolerance=±5% resistance=470 package=THT]
  R17 = Resistor [tolerance=±5% resistance=330 package=THT]
  LED4 = LED - 5mm [color="Red (633nm)" package="5 mm [THT]"]

nets:
  N1: Composant1.D13_PWM, R17.Pin_0
  N2: Composant1.GND, R1.Pin_1, R2.Pin_1, R3.Pin_1, R5.Pin_1, R6.Pin_1, R7.Pin_1, R8.Pin_1, R9.Pin_1, R11.Pin_1, R12.Pin_1, LED1.cathode, LED2.cathode, LED3.cathode, LED4.anode
  N3: Composant1.5V, S1.COM, S2.COM, S3.COM, S4.COM, S5.COM, S6.COM, S7.COM, S8.COM, S9.COM, S10.COM, S11.COM, S12.COM, S13.leg0
  N4: Composant1.D22, R1.Pin_0, S1.L2
  N5: Composant1.D23, R2.Pin_0, S2.L2
  N6: Composant1.D24, R3.Pin_0, S3.L2
  N7: Composant1.D25, R4.Pin_0, S4.L2
  N8: Composant1.D26, R5.Pin_0, S5.L2
  N9: Composant1.D27, R6.Pin_0, S6.L2
  N10: Composant1.D28, R7.Pin_0, S7.L1
  N11: Composant1.D29, R8.Pin_0, S8.L1
  N12: Composant1.D30, R9.Pin_0, S9.L1
  N13: Composant1.D31, R10.Pin_0, S10.L1
  N14: Composant1.D32, R11.Pin_0, S11.L1
  N15: Composant1.D33, R12.Pin_0, S12.L1
  N16: Composant1.D34, S13.leg1, R13.Pin_0
  N17: Composant1.D40, R14.Pin_0
  N18: Composant1.D41, R15.Pin_0
  N19: Composant1.D42, R16.Pin_0
  N20: Composant2.M1-2, M1.pin_2
  N21: Composant2.M1-1, M1.pin_1
  N22: Composant2.M2-2, M2.pin_2
  N23: Composant2.M2-1, M2.pin_1
  GND: Composant2.GND, Power_plug1.GND
  N24: Composant2.M3-2, M3.pin_2
  N25: Composant2.M3-1, M3.pin_1
  VCC: Composant2.VCC, Power_plug1.VCC
  N26: LED1.anode, R14.Pin_1
  N27: LED2.anode, R15.Pin_1
  N28: LED3.anode, R16.Pin_1
  N29: R17.Pin_1, LED4.cathode

// code stored in the sketch: CourseVoiliers.ino
/*  
 *  Course de voiliers
 *  Jérôme Menard
 *  Version 1.0 / Mai 2018
 */

#include <RedMP3.h>
#include <AFMotor.h>

// Déclarations des variables
// Voilier n°1
AF_DCMotor moteur_V1(1);
const byte pinPOSDEPART_V1 = 22;
const byte pinPOSARRIVEE_V1 = 23;
const byte pinPOINT1_V1 = 28;
const byte pinPOINT2_V1 = 29;
const byte pinVICTOIRE_V1 = 34;

// Voilier n°2
AF_DCMotor moteur_V2(2);
const byte pinPOSDEPART_V2 = 24;
const byte pinPOSARRIVEE_V2 = 25;
const byte pinPOINT1_V2 = 30;
const byte pinPOINT2_V2 = 31;
const byte pinVICTOIRE_V2 = 35;

// Voilier n°3
AF_DCMotor moteur_V3(3);
const byte pinPOSDEPART_V3 = 26;
const byte pinPOSARRIVEE_V3 = 27;
const byte pinPOINT1_V3 = 32;
const byte pinPOINT2_V3 = 33;
const byte pinVICTOIRE_V3 = 36;

// Générales
const byte pinBOUTONINIT = 37;
unsigned long tickcount = 0;
unsigned long last_tickcount = 0;


void setup() {
  moteur_V1.run(RELEASE);
  pinMode(pinPOSDEPART_V1, INPUT);
  pinMode(pinPOSARRIVEE_V1, INPUT);
  pinMode(pinPOINT1_V1, INPUT);
  pinMode(pinPOINT2_V1, INPUT);
  pinMode(pinVICTOIRE_V1, OUTPUT);
  moteur_V2.run(RELEASE);
  pinMode(pinPOSDEPART_V2, INPUT);
  pinMode(pinPOSARRIVEE_V2, INPUT);
  pinMode(pinPOINT1_V2, INPUT);
  pinMode(pinPOINT2_V2, INPUT);
  pinMode(pinVICTOIRE_V2, OUTPUT);
  moteur_V3.run(RELEASE);
  pinMode(pinPOSDEPART_V3, INPUT);
  pinMode(pinPOSARRIVEE_V3, INPUT);
  pinMode(pinPOINT1_V3, INPUT);
  pinMode(pinPOINT2_V3, INPUT);
  pinMode(pinVICTOIRE_V3, OUTPUT);

  pinMode(pinBOUTONINIT, INPUT);
}

void loop() {
  tickcount = millis();
  
  boolean boutonInit = digitalRead(pinBOUTONINIT);
  boolean point1_V1 = digitalRead(pinPOINT1_V1);
  
  if (boutonInit == HIGH) {
    initialisationJeu();
  }
  if (point1_V1 == HIGH) {
    moteur_V1.run(FORWARD);
    moteur_V1.setSpeed(100);
    delay(100);
    moteur_V1.run(RELEASE);
  }

  delay(20);
}

void initialisationJeu() {
  boolean departV1 = digitalRead(pinPOSDEPART_V1);
  boolean departV2 = digitalRead(pinPOSDEPART_V2);
  boolean departV3 = digitalRead(pinPOSDEPART_V3);
  do
  {
    departV1 = digitalRead(pinPOSDEPART_V1);
    moteur_V1.run(BACKWARD);
    moteur_V1.setSpeed(200);
    delay(10);
  } while (departV1 == false);
  moteur_V1.run(RELEASE);
  do
  {
    departV2 = digitalRead(pinPOSDEPART_V2);
    moteur_V2.run(BACKWARD);
    moteur_V2.setSpeed(200);
    delay(10);
  } while (departV2 == false);
  moteur_V2.run(RELEASE);
  do
  {
    departV3 = digitalRead(pinPOSDEPART_V3);
    moteur_V3.run(BACKWARD);
    moteur_V3.setSpeed(200);
    delay(10);
  } while (departV3 == false);
  moteur_V2.run(RELEASE);
}

// code stored in the sketch: CourseVoiliers.ino.ino
/*   Course de Voiliers
 *   Jérôme Menard
 *   Version 0.1 - Mai 2018
 */
 
#include <RedMP3.h> 
#include <AFMotor.h>


/*
 * Gestion du son
 */
#define MP3_RX 18
#define MP3_TX 19
MP3 lecteurAudio(MP3_RX, MP3_TX);
int8_t volume = 0x10; // 0~0x1e (niveau ajustable)


/*
 * Clignotement d'une LED
 */
class Flasher
{
  byte ledPin;
  long onTime;
  long offTime;
  int ledState;
  unsigned long previousMillis;
public:
  Flasher(int pin, long on, long off)
  {
    ledPin = pin;
    pinMode(ledPin, OUTPUT);
    onTime = on;
    offTime = off;
    ledState = LOW;
    previousMillis = 0;
  }
  void Update()
  {
    unsigned long currentMillis = millis();
    if ((ledState == HIGH) && (currentMillis - previousMillis >= onTime))
    {
      ledState = LOW;
      previousMillis = currentMillis;
      digitalWrite(ledPin, ledState);
    }
    else if ((ledState == LOW) && (currentMillis - previousMillis >= onTime))
    {
      ledState = HIGH;
      previousMillis = currentMillis;
      digitalWrite(ledPin, ledState);
    }
  }
  void ChangeParameters(long on, long off)
  {
    if (onTime != on) {onTime = on;}
    if (offTime != off) {offTime = off;}
  }
};


/*
 * Gestion des Voiliers
 */
class Voilier
{
  byte indexMotor;
  byte fdcDepartPin;
  byte fdcArriveePin;
  byte ledArriveePin;
  byte fdcTrou1Pin;
  byte fdcTrou2Pin;
  int motorState;
  int motorStateInit;
  unsigned long previousMillis;
public:
  Voilier(byte index, byte pinDepart, byte pinArrivee, byte pinTrou1, byte pinTrou2, byte pinLed)
  {
    indexMotor = index;
    fdcDepartPin = pinDepart;
    pinMode(fdcDepartPin, INPUT);
    fdcArriveePin = pinArrivee;
    pinMode(fdcArriveePin, INPUT);
    fdcTrou1Pin = pinTrou1;
    pinMode(fdcTrou1Pin, INPUT);
    fdcTrou2Pin = pinTrou2;
    pinMode(fdcTrou2Pin, INPUT);
    ledArriveePin = pinLed;
    pinMode(ledArriveePin, OUTPUT);
    motorState = LOW;
    motorStateInit = LOW;
  }
  void RetourAuDepart()
  {
    AF_DCMotor motor(indexMotor);
    if ((motorStateInit == HIGH) && (digitalRead(fdcDepartPin) == HIGH))
    {
      motorStateInit = LOW;
      motor.run(RELEASE);
    }
    else if (motorStateInit == LOW)
    {
      motorStateInit = HIGH;
      motor.setSpeed(200);
      motor.run(BACKWARD);
      lecteurAudio.playWithVolume(0x03,volume);
    }
  }
  void Avance(long onTime)
  {
    AF_DCMotor motor(indexMotor);
    unsigned long currentMillis = millis();
    if (((motorState == HIGH) && (currentMillis - previousMillis >= onTime)) || (digitalRead(fdcArriveePin) == HIGH))
    {
      motorState = LOW;
      motor.run(RELEASE);
    }
    else if ((motorState == LOW) && (digitalRead(fdcArriveePin) == LOW))
    {
      motorState = HIGH;
      previousMillis = currentMillis;
      motor.setSpeed(100);
      motor.run(FORWARD);
      lecteurAudio.playWithVolume(0x01,volume);
    }
  }
  void Update()
  {
    if (motorStateInit == LOW)
    {
      if ((digitalRead(fdcTrou1Pin) == HIGH) || (motorState == HIGH)) {Avance(500);}
      if ((digitalRead(fdcTrou2Pin) == HIGH) || (motorState == HIGH)) {Avance(1000);}
      if (digitalRead(fdcArriveePin) == HIGH)
      {
        Flasher ledArrivee(ledArriveePin, 800, 400);
        lecteurAudio.playWithVolume(0x05,volume);
      }
    }
  }
  int EtatVictoire()
  {
    int arrivee = digitalRead(fdcArriveePin);
    return arrivee;
  }
  int EtatDepart()
  {
    int depart = digitalRead(fdcDepartPin);
    return depart;
  }
  int EtatInit()
  {
    return motorStateInit;
  }
  int EtatMouvement()
  {
    return motorState;
  }
};


/*
 * Variables générales
 */
const byte pinBoutonInit = 37;
Voilier voilier1(1, 22, 23, 28, 29, 34);
Voilier voilier2(2, 24, 25, 30, 31, 35);
Voilier voilier3(3, 26, 27, 32, 33, 36);
Flasher ledActivite(13, 800, 400);
int indexVictoire = 0;


void setup() {
  delay(500);
  pinMode(pinBoutonInit, INPUT);
}


void loop() {
  if ((digitalRead(pinBoutonInit) == HIGH) || (voilier1.EtatInit() == HIGH) || (voilier2.EtatInit() == HIGH) || (voilier3.EtatInit() == HIGH))
  {
    voilier1.RetourAuDepart();
    voilier2.RetourAuDepart();
    voilier3.RetourAuDepart();
    ledActivite.ChangeParameters(80, 40);
   }
  if ((voilier1.EtatDepart() == HIGH) && (voilier1.EtatDepart() == HIGH) && (voilier1.EtatDepart() == HIGH))
  {
    indexVictoire = 0;
    ledActivite.ChangeParameters(800, 400);
  }
  if (indexVictoire ==0)
  {
    if (voilier1.EtatVictoire() == HIGH) {indexVictoire = 1;}
    else if (voilier2.EtatVictoire() == HIGH) {indexVictoire = 2;}
    else if (voilier3.EtatVictoire() == HIGH) {indexVictoire = 3;}
  }
  else
  {
    if (indexVictoire == 1) {digitalWrite(34, HIGH);}
    if (indexVictoire == 2) {digitalWrite(35, HIGH);}
    if (indexVictoire == 3) {digitalWrite(36, HIGH);}
  }
  
  voilier1.Update();
  voilier2.Update();
  voilier3.Update();

  if ((voilier1.EtatMouvement() == HIGH) || (voilier2.EtatMouvement() == HIGH) || (voilier3.EtatMouvement() == HIGH))
  {
    ledActivite.ChangeParameters(80, 40);
  }
  else
  {
    ledActivite.ChangeParameters(800, 400);
  }
  ledActivite.Update();
  
  delay(20);
}
