# Fritzing sketch CourseVoiliers_platineArduino (saved by Fritzing 0.9.3b)
circuit board: 9.8cm x 5.6cm
breadboards: 1

parts:
  J8 = male pin header, 18 pins [form="♂ (male)"]
  J9 = male pin header, 18 pins [form="♂ (male)"]
  J7 = male pin header, 8 pins [form="♂ (male)"]
  J6 = male pin header, 8 pins [form="♂ (male)"]
  J5 = male pin header, 8 pins [form="♂ (male)"]  # not connected
  J3 = male pin header, 8 pins [form="♂ (male)"]
  J4 = male pin header, 8 pins [form="♂ (male)"]
  R1 = Resistor [tolerance=±5% resistance=10k package=THT]
  J10 = female pin header, 8 pins [form="♀ (female)"]
  J11 = female pin header, 8 pins [form="♀ (female)"]
  J12 = female pin header, 8 pins [form="♀ (female)"]
  J14 = female pin header, 8 pins [form="♀ (female)"]
  R2 = Resistor [tolerance=±5% resistance=10k package=THT]
  R3 = Resistor [tolerance=±5% resistance=10k package=THT]
  R4 = Resistor [tolerance=±5% resistance=10k package=THT]
  R5 = Resistor [tolerance=±5% resistance=10k package=THT]
  R6 = Resistor [tolerance=±5% resistance=10k package=THT]
  R7 = Resistor [tolerance=±5% resistance=10k package=THT]
  R8 = Resistor [tolerance=±5% resistance=10k package=THT]
  R9 = Resistor [tolerance=±5% resistance=10k package=THT]
  R10 = Resistor [tolerance=±5% resistance=10k package=THT]
  R11 = Resistor [tolerance=±5% resistance=10k package=THT]
  R12 = Resistor [tolerance=±5% resistance=10k package=THT]
  R13 = Resistor [tolerance=±5% resistance=10k package=THT]
  R14 = Resistor [tolerance=±5% resistance=470 package=THT]
  R15 = Resistor [tolerance=±5% resistance=470 package=THT]
  R16 = Resistor [tolerance=±5% resistance=470 package=THT]
  R17 = Resistor [tolerance=±5% resistance=330 package=THT]
  S1 = Pushbutton [package=THT]
  S2 = Pushbutton [package=THT]
  S3 = Pushbutton [package=THT]
  S4 = Pushbutton [package=THT]
  S5 = Pushbutton [package=THT]
  S6 = Pushbutton [package=THT]
  S7 = Pushbutton [package=THT]
  S8 = Pushbutton [package=THT]
  S9 = Pushbutton [package=THT]
  S10 = Pushbutton [package=THT]
  S11 = Pushbutton [package=THT]
  S12 = Pushbutton [package=THT]
  LED1 = LED - 5mm [color="Green (570nm)" package="5 mm [THT]"]
  LED2 = LED - 5mm [color="Green (570nm)" package="5 mm [THT]"]
  LED3 = LED - 5mm [color="Green (570nm)" package="5 mm [THT]"]
  LED4 = LED - 5mm [color="Red (633nm)" package="5 mm [THT]"]
  S13 = Pushbutton [package=THT]
  J15 = female pin header, 8 pins [form="♀ (female)"]
  J2 = male pin header, 10 pins [form="♂ (male)"]

nets:
  N1: J8.pin1, J9.pin1, J3.pin6, J3.pin7, R1.Pin_1, J10.pin6, J10.pin7, J14.pin2, R2.Pin_1, R3.Pin_1, R4.Pin_1, R5.Pin_1, R6.Pin_1, R7.Pin_1, R8.Pin_1, R9.Pin_1, R10.Pin_1, R11.Pin_1, R12.Pin_1, R13.Pin_1, LED1.anode, LED2.anode, LED3.anode, LED4.anode, J2.pin4
  N2: J8.pin5, R17.Pin_0
  N3: J8.pin9, R16.Pin_0
  N4: J8.pin13, R15.Pin_0
  N5: J8.pin17, R14.Pin_0
  N6: J8.pin18, J9.pin18, J3.pin5, J10.pin5, S1.leg1, S2.leg1, S3.leg1, S4.leg1, S5.leg1, S6.leg1, S7.leg1, S8.leg1, S9.leg1, S10.leg1, S11.leg1, S12.leg1, S13.leg1
  N7: J9.pin5, R13.Pin_0, S13.leg0
  N8: J9.pin6, R12.Pin_0, S12.leg0
  N9: J9.pin7, R11.Pin_0, S11.leg0
  N10: J9.pin8, R10.Pin_0, S10.leg0
  N11: J9.pin9, R9.Pin_0, S9.leg0
  N12: J9.pin10, R8.Pin_0, S8.leg0
  N13: J9.pin11, R7.Pin_0, S7.leg0
  N14: J9.pin12, R6.Pin_0, S6.leg0
  N15: J9.pin13, R5.Pin_0, S5.leg0
  N16: J9.pin14, R4.Pin_0, S4.leg0
  N17: J9.pin15, R3.Pin_0, S3.leg0
  N18: J9.pin16, R2.Pin_0, S2.leg0
  N19: J9.pin17, R1.Pin_0, S1.leg0
  N20: J7.pin1, J12.pin1
  N21: J7.pin2, J12.pin2
  N22: J7.pin3, J12.pin3
  N23: J7.pin4, J12.pin4
  N24: J7.pin5, J12.pin5
  N25: J7.pin6, J12.pin6
  N26: J7.pin7, J12.pin7
  N27: J7.pin8, J12.pin8
  N28: J6.pin1, J15.pin1
  N29: J6.pin2, J15.pin2
  N30: J6.pin3, J15.pin3
  N31: J6.pin4, J15.pin4
  N32: J6.pin5, J15.pin5
  N33: J6.pin6, J15.pin6
  N34: J6.pin7, J15.pin7
  N35: J6.pin8, J15.pin8
  N36: J3.pin1, J10.pin1
  N37: J3.pin2, J10.pin2
  N38: J3.pin3, J10.pin3
  N39: J3.pin4, J10.pin4
  N40: J3.pin8, J10.pin8
  N41: J4.pin1, J11.pin1
  N42: J4.pin2, J11.pin2
  N43: J4.pin3, J11.pin3
  N44: J4.pin4, J11.pin4
  N45: J4.pin5, J11.pin5
  N46: J4.pin6, J11.pin6
  N47: J4.pin7, J11.pin7
  N48: J4.pin8, J11.pin8
  N49: J14.pin1, J2.pin3
  N50: J14.pin3, J2.pin5
  N51: J14.pin4, J2.pin6
  N52: J14.pin5, J2.pin7
  N53: J14.pin6, J2.pin8
  N54: J14.pin7, J2.pin9
  N55: J14.pin8, J2.pin10
  N56: R14.Pin_1, LED1.cathode
  N57: R15.Pin_1, LED2.cathode
  N58: R16.Pin_1, LED3.cathode
  N59: R17.Pin_1, LED4.cathode
